# Fritzing sketch wiring_diagram (saved by Fritzing 0.9.3b)
breadboards: 1

parts:
  Raspberry_Pi_1 = Raspberry Pi 3 [part_number=RPI-3-V1.2]
  LED1 = LED - 5mm [color="Red (633nm)" package="5 mm [THT]"]
  Part1 = Adafruit VCNL4010 Proximity and Light sensor [part_number="Adafruit #466"]
  R1 = Resistor [tolerance=±5% resistance=330 package=THT]

nets:
  3V3: Raspberry_Pi_1.3v3, Part1.VIN
  N1: Raspberry_Pi_1.GPIO2, Part1.SDA
  N2: Raspberry_Pi_1.GPIO3, Part1.SCL
  GND: Raspberry_Pi_1.GND, LED1.cathode, Part1.GND
  N3: Raspberry_Pi_1.GPIO17, R1.Pin_1
  N4: LED1.anode, R1.Pin_0

notes:
  Add PiCamera in Camera slot

custom parts:
  Adafruit VCNL4010 Proximity and Light sensor: The VCNL4010 sensor is a nice way to add a small-distance proximity sensor to your microcontroller project. For longer distances (in the range of cm, you can use a SHARP IR distance sensor, but those are only good if the object is over 10 cm away. The VCNL4010 is designed for much shorter distances, no more than 200mm (about 7.5") and under our experimentation we found it worked best at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
